# Fritzing sketch Hardware_v1_emitterCircuit (saved by Fritzing 0.9.3b)
circuit board: 7.78802cm x 4.62171cm
perfboards: 1

parts:
  R1 = Resistor [tolerance=±5% resistance=120 package=THT]
  GND = BANANA_CONN [package=banana_conn]
  Cin = Ceramic Capacitor [capacitance=100nF package="100 mil [THT, multilayer]"]
  Cout = Ceramic Capacitor [capacitance=100nF package="100 mil [THT, multilayer]"]
  +24V = BANANA_CONN [package=banana_conn]
  ServoCon = Header 3 [package=molex-1x3_lock]
  +Motor = Header 2 [package=molex-1x2_lock]
  -Motor = Header 2 [package=molex-1x2_lock]
  +5V_Ctrl = Voltage Regulator - 5V [package="TO220 [THT]"]
  FET1 = MOSFET-NCHANNEL [package=to220v]
  ArduinoNano = Arduino Nano (Rev3.0) (ICSP)

nets:
  N1: R1.Pin_0, ArduinoNano.D9
  N2: R1.Pin_1, FET1.G
  GND: GND.1, Cin.0, Cout.0, ServoCon.3, +5V_Ctrl.GND, FET1.S, ArduinoNano.GND
  24V: Cin.1, +24V.1, +Motor.1, +Motor.2, +5V_Ctrl.input_voltage
  5V: Cout.1, ServoCon.2, +5V_Ctrl.output_voltage, ArduinoNano.VIN
  N3: ServoCon.1, ArduinoNano.D2
  N4: -Motor.1, -Motor.2, FET1.D
