# Fritzing sketch Hardware_v3_Fullbridge_lowpass (saved by Fritzing 0.9.3b)
circuit board: 4.47018cm x 4.65312cm

parts:
  R1 = Resistor [tolerance=±5% resistance=120 package=THT]
  GND = BANANA_CONN [package=banana_conn]
  +24V = BANANA_CONN [package=banana_conn]
  ServoCon = Header 3 [package=molex-1x3_lock]
  +Motor = Header 2 [package=molex-1x2_lock]
  -Motor = Header 2 [package=molex-1x2_lock]
  L+ = MOSFET-NCHANNEL [part_number=IRF1010N package=to220v]
  L- = MOSFET-NCHANNEL [part_number=IRF1010N package=to220v]
  C1 = Electrolytic Capacitor [capacitance=0.22mF package="100 mil [THT, electrolytic]"]
  C2 = Electrolytic Capacitor [capacitance=0.22mF package="100 mil [THT, electrolytic]"]
  R2 = Resistor [tolerance=±5% resistance=120 package=THT]
  R3 = Resistor [tolerance=±5% resistance=1k package=THT]
  R4 = Resistor [tolerance=±5% resistance=1k package=THT]
  H+ = Basic FET P-Channel [part_number=IRF5305 package="TO220 [THT]"]
  H- = Basic FET P-Channel [part_number=IRF5305 package="TO220 [THT]"]
  R5 = Resistor [tolerance=±5% resistance=4.7k package=THT]
  R6 = Resistor [tolerance=±5% resistance=4.7k package=THT]
  R7 = Resistor [tolerance=±5% resistance=15k package=THT]
  R8 = Resistor [tolerance=±5% resistance=15k package=THT]
  NPN+ = NPN-Transistor [part_number=BC635 package="TO92 [THT]"]
  NPN- = NPN-Transistor [part_number=BC635 package="TO92 [THT]"]
  Arduino = Arduino Nano (Rev3.0)
  5V_StepDownConverter = RioRand LM2596
  R9 = Resistor [tolerance=±5% resistance=7 package=THT]
  C3 = Electrolytic Capacitor [capacitance=330µF package="100 mil [THT, electrolytic]"]

nets:
  N1: R1.Pin_0, Arduino.D9
  N2: R1.Pin_1, L+.G, R7.Pin_0
  GND: GND.1, ServoCon.3, L+.S, L-.S, C2.-, R7.Pin_1, R8.Pin_1, NPN+.E, NPN-.E, Arduino.GND, 5V_StepDownConverter.Pin_2, 5V_StepDownConverter.Pin_4, C3.-
  24V: +24V.1, C1.+, H+.source, H-.source, R5.Pin_1, R6.Pin_1, 5V_StepDownConverter.Pin_1
  N3: ServoCon.1, Arduino.D2
  5V: ServoCon.2, Arduino.VIN, R9.Pin_1, C3.+
  N4: +Motor.1, +Motor.2, L+.D, H+.drain
  N5: -Motor.1, -Motor.2, L-.D, H-.drain
  N6: L-.G, R2.Pin_1, R8.Pin_0
  N7: C1.-, C2.+
  N8: R2.Pin_0, Arduino.D10
  N9: R3.Pin_0, Arduino.D7
  N10: R3.Pin_1, NPN+.B
  N11: R4.Pin_0, Arduino.D8
  N12: R4.Pin_1, NPN-.B
  N13: H+.gate, R5.Pin_0, NPN+.C
  N14: H-.gate, R6.Pin_0, NPN-.C
  N15: 5V_StepDownConverter.Pin_3, R9.Pin_0
